# Fritzing sketch infotron (saved by Fritzing 0.9.3b)

parts:
  A1 = MH-ET Live Minikit for ESP32
  M1 = MAX7219 8x8 single Led Matrix Module
  M2 = MAX7219 8x8 single Led Matrix Module  # not connected
  M3 = MAX7219 8x8 single Led Matrix Module  # not connected
  M4 = MAX7219 8x8 single Led Matrix Module  # not connected

nets:
  N1: A1.GND, M1.I-GND
  N2: A1.IO18, M1.I-CLK, M1.O-CLK
  N3: A1.IO23, M1.I-DIN
  N4: A1.IO5, M1.I-CS, M1.O-CS
  N5: A1.3.3V, M1.I-VCC, M1.O-VCC

notes:
  DIN
  IO23
  CS
  IO5
  CLK
  IO18
  GND
  3.3V
  VCC
  LED disp.
  ESP32

custom parts:
  MH-ET Live Minikit for ESP32: MH-ET Live Minikit for ESP32 ( http://mh.nodebb.com/topic/8/mh-et-live-minikit-for-esp32/2/) PCB footprint is invalid.
  MAX7219 8x8 single Led Matrix Module: Description: MAX7219 8x8 LedMatrix single Red Module Dimensions: 32x32mm Documents:
